# Fritzing sketch driver (saved by Fritzing 0.9.3b)
circuit board: 4.5cm x 2.5cm
breadboards: 1

parts:
  C1 = Electrolytic Capacitor [capacitance=1µF package="100 mil [THT, electrolytic]"]
  R1 = Resistor [tolerance=±5% resistance=10k package=THT]
  R2 = Resistor [tolerance=±5% resistance=1.5M package=THT]
  R3 = Resistor [tolerance=±5% resistance=1.5M package=THT]
  R4 = Resistor [tolerance=±5% resistance=220 package=THT]
  R5 = Resistor [tolerance=±5% resistance=330 package=THT]
  R6 = Resistor [tolerance=±5% resistance=330 package=THT]
  S1 = Pushbutton [package="[THT]"]
  R7 = Resistor [tolerance=±5% resistance=51k package=THT]
  R8 = Resistor [tolerance=±5% resistance=100 package=THT]
  Q1 = MOSFET-NCHANNEL [package=to220v]
  LED_CON = female pin header, 2 pins [form="♀ (female)"]
  C2 = Electrolytic Capacitor [capacitance=10µF package="100 mil [THT, electrolytic]"]
  BAT_CON = female pin header, 2 pins [form="♀ (female)"]
  U1 = ATTINY13 [package=so]
  LED1 = LED - 3mm [color="Red (633nm)" package="3 mm [THT]"]

nets:
  GND: C1.-, R4.Pin_1, S1.Pin_3, S1.Pin_4, R7.Pin_0, Q1.S, C2.-, BAT_CON.pin2, U1.GND
  Vcc/Vin: C1.+, R1.Pin_1, R2.Pin_1, R3.Pin_1, LED_CON.pin1, C2.+, BAT_CON.pin1, U1.VCC
  N1: R1.Pin_0, U1.PB5(NRES)
  N2: R2.Pin_0, R3.Pin_0, R4.Pin_0, U1.PB4(ADC2), LED1.cathode
  N3: R5.Pin_0, U1.PB2(SCK_ADC1)
  N4: R5.Pin_1, LED1.anode
  N5: R6.Pin_0, S1.Pin_1, S1.Pin_2
  BTN: R6.Pin_1, U1.PB1(MISO)
  LOAD: R7.Pin_1, R8.Pin_1, U1.PB0(MOSI)
  N6: R8.Pin_0, Q1.G
  N7: Q1.D, LED_CON.pin2
