# Fritzing sketch feather (saved by Fritzing 0.9.3b)
breadboards: 1

parts:
  J1 = female pin header, 16 pins [form="♀ (female)"]
  J2 = female pin header, 12 pins [form="♀ (female)"]

nets:
  RST: J1.pin1
  3V3_OUT: J1.pin2
  AREF/NC: J1.pin3
  GND: J1.pin4
  A0: J1.pin5
  A1: J1.pin6
  A2: J1.pin7
  A3: J1.pin8
  A4: J1.pin9
  A5: J1.pin10
  SCK: J1.pin11
  MOSI: J1.pin12
  MISO: J1.pin13
  RX: J1.pin14
  TX: J1.pin15
  FREE/IO/DFU/GND: J1.pin16
  BAT: J2.pin1
  EN: J2.pin2
  BUS: J2.pin3
  D13: J2.pin4
  D12: J2.pin5
  D11: J2.pin6
  D10: J2.pin7
  D9: J2.pin8
  D6: J2.pin9
  D5: J2.pin10
  SCL: J2.pin11
  SDA: J2.pin12
